# Fritzing sketch SensorCircuit_On-perfBoard (saved by Fritzing 1.0.0rc)
perfboards: 1

parts:
  J1 = Screw terminal - 2 pins [package=THT]
  LED1 = LED - 5mm [color="Green (560nm)" current=0.030A package="5 mm [THT]"]
  S1 = Toggle Switch [package=THT]
  IC1 = IC, DIP package, 14 pins [chip_label="ATTiny 84"]  # not connected
  Part1 = NRF24L01+ Breakout Board
  R1 = Resistor [tolerance=±5% power=0.25W resistance=220 package=THT]
  C1 = Electrolytic Capacitor [capacitance=10µF voltage=35V mpn=10 package="100 mil [THT, electrolytic]"]
  J2 = screw terminal, 2 pins  # not connected
  LED2 = LED - 5mm [color="Red (633nm)" current=0.030A package="5 mm [THT]"]
  R2 = Resistor [tolerance=±5% power=0.25W resistance=220 package=THT]

nets:
  N1: J1.pin1, LED1.cathode, Part1.GND, C1.-, LED2.cathode
  N2: J1.pin2, S1.L1
  N3: LED1.anode, R1.Pin_0
  N4: S1.COM, C1.+
  N5: LED2.anode, R2.Pin_0

custom parts:
  NRF24L01+ Breakout Board: This breakout board is for the Nordic Semiconductor NRF24L01+ 2.4GHz RF transceiver IC.
